# Fritzing sketch AR (saved by Fritzing 0.8.3b)
breadboards: 1

parts:
  Componente1 = Arduino Uno (Rev3)
  U1 = POT [package=pot_alpha_rv16af-20]
  LED1 = RGB LED - (4 legs) [package="5 mm [THT]"]
  Q2 = Basic FET N-Channel [package="TO220 [THT]"]
  M1 = DC Motor
  U2 = HEF4543 [package=dil16]
  R1 = Temperature Sensor (Thermistor) [thermistor_type=NTC package=THT]
  R4 = Resistor [tolerance=±5% resistance=270 package=THT]
  R5 = Resistor [tolerance=±5% resistance=270 package=THT]
  R6 = Resistor [tolerance=±5% resistance=270 package=THT]
  DI1 = 7-Segment LED Display [package=THT]
  R7 = Resistor [tolerance=±5% resistance=270 package=THT]
  R8 = Resistor [tolerance=±5% resistance=10k package=THT]
  R9 = Resistor [tolerance=±5% resistance=270 package=THT]

nets:
  N1: Componente1.A0, R1.pin_0, R8.Pin_0
  N2: Componente1.A2, U1.S
  N3: Componente1.ICSP_SCK, Componente1.D13/SCK, R9.Pin_1
  GND: Componente1.GND, U1.A, LED1.common_anode, M1.pin_2, U2.D0, U2.GND, R8.Pin_1
  N4: Componente1.D9_PWM, U2.PH
  N5: Componente1.D10_PWM/SS, U2.LD
  N6: Componente1.D11_PWM/MOSI, U2.D2
  N7: Componente1.D12/MISO, U2.BL
  N8: Componente1.D2, R6.Pin_1
  N9: Componente1.D3_PWM, R4.Pin_1
  N10: Componente1.D4, R5.Pin_1
  N11: Componente1.D7, Q2.gate
  5V: Componente1.5V, U1.E, U2.D1, U2.D3, U2.VCC, R7.Pin_1
  N12: Componente1.VIN, Q2.drain
  N13: LED1.red_cathode, R6.Pin_0
  N14: LED1.green_cathode, R4.Pin_0
  N15: LED1.blue_cathode, R5.Pin_0
  N16: Q2.source, M1.pin_1
  N17: U2.A, DI1.cathodeE
  N18: U2.B, DI1.cathodeD
  N19: U2.C, DI1.cathodeC
  N20: U2.D, DI1.cathodeB
  N21: U2.E, DI1.cathodeA
  N22: U2.G, DI1.cathodeG
  N23: U2.F, DI1.cathodeF
  N24: DI1.commAnode#2, R7.Pin_0
  N25: DI1.cathodeDP, R9.Pin_0
